// Logisim project 4Bit_Counter.circ as structural Verilog: 1 circuit, main circuit main
module main (
);

  wire and_1_out, and_2_out, and_3_out, and_4_out, and_5_out, and_6_out, and_7_out, and_8_out, and_9_out,
       and_10_out, and_11_out, and_12_out, CLK, DA, DB, DC, DD, ENP, ENT, nand_1_out, nand_2_out, nand_3_out,
       nand_5_out, nand_7_out, nand_8_out, NCLR, NLOAD, not_1_out, not_2_out, not_3_out, or_1_out, or_2_out,
       or_3_out, or_4_out, or_5_out, QA, QB, QC, QD, RCO;

  not not_1 (not_1_out, NCLR);
  and and_1 (and_1_out, ENP, ENT);
  not not_2 (not_2_out, NLOAD);
  not not_3 (not_3_out, not_1_out);
  or or_1 (or_1_out, not_2_out, not_3_out);
  and and_2 (and_2_out, QA, and_1_out);
  and and_3 (and_3_out, QA, QB, and_1_out);
  and and_4 (and_4_out, QA, QB, QC, and_1_out);
  nand nand_1 (nand_1_out, or_1_out, nand_2_out);
  nand nand_2 (nand_2_out, DA, not_1_out, or_1_out);
  nand nand_3 (nand_3_out, or_1_out, and_2_out);
  nand nand_4 (and_2_out, DB, not_1_out, or_1_out);
  nand nand_5 (nand_5_out, or_1_out, and_3_out);
  nand nand_6 (and_3_out, DC, not_1_out, or_1_out);
  nand nand_7 (nand_7_out, or_1_out, nand_8_out);
  nand nand_8 (nand_8_out, or_1_out, DD, not_1_out);
  or or_2 (or_2_out, and_1_out, or_1_out);
  or or_3 (or_3_out, and_2_out, or_1_out);
  or or_4 (or_4_out, and_3_out, or_1_out);
  or or_5 (or_5_out, and_4_out, or_1_out);
  and and_5 (and_5_out, nand_1_out, or_2_out);
  and and_6 (and_6_out, or_2_out, nand_2_out);
  and and_7 (and_7_out, nand_3_out, or_3_out);
  and and_8 (and_8_out, or_3_out, and_2_out);
  and and_9 (and_9_out, nand_5_out, or_4_out);
  and and_10 (and_10_out, or_4_out, and_3_out);
  and and_11 (and_11_out, nand_7_out, or_5_out);
  and and_12 (and_12_out, or_5_out, nand_8_out);
  J_K_Flip_Flop j_k_ff_1 (.J(and_5_out), .K(and_6_out), .clk(CLK), .Q(QA));  // open: Qn, preset, reset
  J_K_Flip_Flop j_k_ff_2 (.J(and_7_out), .K(and_8_out), .clk(CLK), .Q(QB));  // open: Qn, preset, reset
  J_K_Flip_Flop j_k_ff_3 (.J(and_9_out), .K(and_10_out), .clk(CLK), .Q(QC));  // open: Qn, preset, reset
  J_K_Flip_Flop j_k_ff_4 (.J(and_11_out), .K(and_12_out), .clk(CLK), .Q(QD));  // open: Qn, preset, reset
  and and_13 (RCO, QD, QA, QB, QC, ENT);
endmodule
