// Logisim project 8Bit_Computer.circ as structural Verilog: 13 circuits, main circuit ProgCounter
module main (
);

  wire AI, AO, BI, Carry, CE, CF, CLK, CO, EO, FI, HLT, II, IO, J, MI, OI, RI, RO, RST, SU, ZF;
  wire [3:0] LogBus, memoryaddressregister_1_ramaddrout;
  wire [7:0] ALUA, ALUB, aregister_1_busout, ZFCompare;

  // Switch switch_1: pin names not known; wires that end beside it: 1'b1, RST
  ClockCircuit clockcircuit_1 (.CLKOut(CLK), .HLT(HLT));
  ARegister aregister_1 (
    .ToALUa(ALUA), .BusOut(aregister_1_busout), .AI(AI), .BusIn(aregister_1_busout), .CLK(CLK), .RST(RST),
    .AO(AO));
  BRegister bregister_1 (.ToALUb(ALUB), .BI(BI), .BusIn(aregister_1_busout), .CLK(CLK), .RST(RST));
  FlagsRegister flagsregister_1 (
    .CF(CF), .ZF(ZF), .AdderCarry(Carry), .FI(FI), .CLK(CLK), .RST(RST), .ZFCompare(ZFCompare));
  ALU alu_1 (
    .Carry(Carry), .ZFCompare(ZFCompare), .BusOut(aregister_1_busout), .ARegisterIn(ALUA),
    .BRegisterIn(ALUB), .EO(EO), .SU(SU));  // open: SubCarry
  InstructionRegister instructionregister_1 (
    .LogBusOut(LogBus), .BusOut(aregister_1_busout), .II(II), .CLK(CLK), .BusIn(aregister_1_busout),
    .RST(RST), .IO(IO));
  BusDisplay busdisplay_1 (.BusIn(aregister_1_busout));
  OutputRegister outputregister_1 (.CLK(CLK), .RST(RST), .OI(OI), .BusIn(aregister_1_busout));
  ProgCounter progcounter_1 (
    .BusOut(aregister_1_busout), .BusIn(aregister_1_busout), .CLK(CLK), .CE(CE), .J(J), .RST(RST), .CO(CO));
  MemoryAddressRegister memoryaddressregister_1 (
    .RamAddrOut(memoryaddressregister_1_ramaddrout), .BusIn(aregister_1_busout), .MI(MI), .CLK(CLK), .RST(RST));
  RandomAccessMemory randomaccessmemory_1 (
    .BusOut(aregister_1_busout), .RI(RI), .RO(RO), .CLK(CLK), .BusIn(aregister_1_busout),
    .RamAddrIn(memoryaddressregister_1_ramaddrout));
  ControlLogic controllogic_1 (
    .AO(AO), .FI(FI), .AI(AI), .J(J), .II(II), .CO(CO), .IO(IO), .CE(CE), .RO(RO), .OI(OI), .RI(RI), .BI(BI),
    .MI(MI), .SU(SU), .HLT(HLT), .EO(EO), .RST(RST), .CLK(CLK), .LogBusIn(LogBus), .CF(CF), .ZF(ZF),
    .BusOut(aregister_1_busout));

  // Notes on the sheet:
  //   Master Reset
endmodule

module ProgCounter (
  input  CLK,
  input  CE,
  input  J,
  input  RST,
  input  [7:0] BusIn,
  input  CO,
  output [7:0] BusOut
);

  wire [3:0] counter_1_q;

  LED led_1 (.in(CLK));
  // NoConnect on BusIn[7:4]
  LED led_2 (.in(CE));
  LED led_3 (.in(J));
  LED led_4 (.in(RST));
  Counter #(.max('hf), .width(4)) counter_1 (
    .clr(RST), .load(J), .up(1'b1), .count(CE), .clk(CLK), .D(BusIn[3:0]), .Q(counter_1_q));  // open: carry
  LED led_5 (.in(CO));
  LED led_6 (.in(counter_1_q[3]));
  LED led_7 (.in(counter_1_q[2]));
  assign BusOut[7] = CO ? 1'b0 : 1'bz;  // Controlled_Buffer controlled_buffer_1
  LED led_8 (.in(counter_1_q[1]));
  LED led_9 (.in(counter_1_q[0]));
  assign BusOut[4] = CO ? 1'b0 : 1'bz;  // Controlled_Buffer controlled_buffer_2
  assign BusOut[5] = CO ? 1'b0 : 1'bz;  // Controlled_Buffer controlled_buffer_3
  assign BusOut[6] = CO ? 1'b0 : 1'bz;  // Controlled_Buffer controlled_buffer_4
  assign BusOut[1] = CO ? counter_1_q[1] : 1'bz;  // Controlled_Buffer controlled_buffer_5
  assign BusOut[2] = CO ? counter_1_q[2] : 1'bz;  // Controlled_Buffer controlled_buffer_6
  assign BusOut[3] = CO ? counter_1_q[3] : 1'bz;  // Controlled_Buffer controlled_buffer_7
  assign BusOut[0] = CO ? counter_1_q[0] : 1'bz;  // Controlled_Buffer controlled_buffer_8
endmodule

module ARegister (
  input  [7:0] BusIn,
  input  AI,
  input  AO,
  input  CLK,
  input  RST,
  output [7:0] ToALUa,
  output [7:0] BusOut
);

  LED led_1 (.in(AI));
  LED led_2 (.in(CLK));
  Register A (.D(BusIn), .en(AI), .clk(CLK), .Q(ToALUa), .clr(RST));
  LED led_3 (.in(RST));
  assign BusOut = AO ? ToALUa : 8'bz;  // Controlled_Buffer controlled_buffer_1
  LED led_4 (.in(AO));
endmodule

module BRegister (
  input  [7:0] BusIn,
  input  BI,
  input  CLK,
  input  RST,
  output [7:0] ToALUb
);

  LED led_1 (.in(BI));
  LED led_2 (.in(CLK));
  Register B (.D(BusIn), .en(BI), .clk(CLK), .Q(ToALUb), .clr(RST));
  LED led_3 (.in(RST));
endmodule

module InstructionRegister (
  input  [7:0] BusIn,
  input  II,
  input  CLK,
  input  IO,
  input  RST,
  output [7:0] BusOut,
  output [3:0] LogBusOut
);

  wire [3:0] I_q;

  LED led_1 (.in(II));
  Register I (.D(BusIn), .en(II), .clk(CLK), .Q({LogBusOut, I_q}), .clr(RST));
  LED led_2 (.in(CLK));
  LED led_3 (.in(RST));
  assign BusOut = IO ? {4'b0000, I_q} : 8'bz;  // Controlled_Buffer controlled_buffer_1
  LED led_4 (.in(IO));
endmodule

module ClockCircuit (
  input  HLT,
  output CLKOut
);

  wire CLK_out, nand_1_out;

  Clock #(.highDuration(4), .lowDuration(4)) CLK (.out(CLK_out));
  and and_1 (CLKOut, CLK_out, nand_1_out);
  LED led_1 (.in(CLKOut));
  nand nand_1 (nand_1_out, HLT, HLT);
  Pull_Resistor pull_resistor_1 (.node(HLT));
endmodule

module FlagsRegister (
  input  AdderCarry,
  input  [7:0] ZFCompare,
  input  FI,
  input  CLK,
  input  RST,
  output CF,
  output ZF
);

  wire [1:1] comparator_1_eq;

  LED led_1 (.in(AdderCarry));
  LED led_2 (.in(FI));
  LED led_3 (.in(CLK));
  Register #(.width(2)) register_1 (.D({comparator_1_eq[1], AdderCarry}), .en(FI), .clk(CLK), .Q({ZF, CF}), .clr(RST));
  LED led_4 (.in(RST));
  Comparator #(.mode("unsigned")) comparator_1 (.a({8{1'b0}}), .b(ZFCompare), .eq(comparator_1_eq[1]));  // open: gt, lt
  LED led_5 (.in(CF));
  LED led_6 (.in(ZF));
endmodule

module ALU (
  input  [7:0] ARegisterIn,
  input  [7:0] BRegisterIn,
  input  SU,
  input  EO,
  output [7:0] ZFCompare,
  output Carry,
  output [7:0] BusOut,
  output SubCarry
);

  wire [7:0] controlled_buffer_1_out, controlled_buffer_2_out, subtractor_1_out;

  LED led_1 (.in(SubCarry));
  LED led_2 (.in(Carry));
  LED led_3 (.in(subtractor_1_out[0]));
  LED led_4 (.in(subtractor_1_out[1]));
  LED led_5 (.in(subtractor_1_out[2]));
  LED led_6 (.in(subtractor_1_out[3]));
  LED led_7 (.in(subtractor_1_out[4]));
  LED led_8 (.in(subtractor_1_out[5]));
  LED led_9 (.in(subtractor_1_out[6]));
  LED led_10 (.in(subtractor_1_out[7]));
  Adder adder_1 (.a(ARegisterIn), .b(BRegisterIn), .out(ZFCompare), .cout(Carry));  // open: cin
  LED led_11 (.in(ZFCompare[0]));
  LED led_12 (.in(ZFCompare[1]));
  LED led_13 (.in(ZFCompare[2]));
  LED led_14 (.in(ZFCompare[3]));
  LED led_15 (.in(ZFCompare[4]));
  LED led_16 (.in(ZFCompare[5]));
  LED led_17 (.in(ZFCompare[6]));
  LED led_18 (.in(ZFCompare[7]));
  Subtractor subtractor_1 (.a(ARegisterIn), .b(BRegisterIn), .out(subtractor_1_out), .bout(SubCarry));  // open: bin
  assign controlled_buffer_1_out = EO ? ZFCompare : 8'bz;  // Controlled_Buffer controlled_buffer_1
  assign controlled_buffer_2_out = EO ? subtractor_1_out : 8'bz;  // Controlled_Buffer controlled_buffer_2
  Multiplexer #(.enable("false"), .width(8)) multiplexer_1 (
    .in0(controlled_buffer_1_out), .in1(controlled_buffer_2_out), .out(BusOut), .sel(SU));
  LED led_19 (.in(SU));
  LED led_20 (.in(EO));
endmodule

module BusDisplay (
  input  [7:0] BusIn
);

  wire bcd_to_7_segment_decoder_3_p1, binary_to_bcd_converter_1_p2, binary_to_bcd_converter_1_p4;

  Hex_Digit_Display hex_digit_display_1 (.value(BusIn[7:4]));  // open: dp
  Hex_Digit_Display hex_digit_display_2 (.value(BusIn[3:0]));  // open: dp
  _7_Segment_Display u_7_segment_display_1 ();  // open: g, f, a, b, e, d, c, dp
  // BCD_to_7_Segment_decoder bcd_to_7_segment_decoder_1: pin names not known
  // Binary_to_BCD_converter #(.binvalue(8)) binary_to_bcd_converter_1: pin names not known; wires that end beside it: BusIn, binary_to_bcd_converter_1_p2, binary_to_bcd_converter_1_p2, binary_to_bcd_converter_1_p4
  LED led_1 (.in(BusIn[0]));
  LED led_2 (.in(BusIn[1]));
  LED led_3 (.in(BusIn[2]));
  LED led_4 (.in(BusIn[3]));
  LED led_5 (.in(BusIn[4]));
  LED led_6 (.in(BusIn[5]));
  LED led_7 (.in(BusIn[6]));
  LED led_8 (.in(BusIn[7]));
  _7_Segment_Display u_7_segment_display_2 ();  // open: g, f, a, b, e, d, c, dp
  // BCD_to_7_Segment_decoder bcd_to_7_segment_decoder_2: pin names not known; wires that end beside it: binary_to_bcd_converter_1_p4
  _7_Segment_Display u_7_segment_display_3 ();  // open: g, f, a, b, e, d, c, dp
  // BCD_to_7_Segment_decoder bcd_to_7_segment_decoder_3: pin names not known; wires that end beside it: bcd_to_7_segment_decoder_3_p1, bcd_to_7_segment_decoder_3_p1
endmodule

module MemoryAddressRegister (
  input  [7:0] BusIn,
  input  MI,
  input  CLK,
  input  RST,
  output [3:0] RamAddrOut
);

  LED led_1 (.in(MI));
  // NoConnect on BusIn[7:4]
  LED led_2 (.in(CLK));
  LED led_3 (.in(RST));
  Register #(.width(4)) MR (.D(BusIn[3:0]), .en(MI), .clk(CLK), .Q(RamAddrOut), .clr(RST));
endmodule

module RandomAccessMemory (
  input  [3:0] RamAddrIn,
  input  RI,
  input  RO,
  input  CLK,
  input  [7:0] BusIn,
  output [7:0] BusOut
);

  wire [7:0] controlled_buffer_1_out, ram_1_dout;

  LED led_1 (.in(RI));
  LED led_2 (.in(RO));
  LED led_3 (.in(CLK));
  assign controlled_buffer_1_out = RI ? BusIn : 8'bz;  // Controlled_Buffer controlled_buffer_1
  assign BusOut = RO ? ram_1_dout : 8'bz;  // Controlled_Buffer controlled_buffer_2
  RAM #(.addrWidth(4), .asyncread("true")) ram_1 (
    .addr(RamAddrIn), .we(RI), .oe(RO), .clk(CLK), .din(controlled_buffer_1_out), .dout(ram_1_dout));
endmodule

module OutputRegister (
  input  [7:0] BusIn,
  input  OI,
  input  CLK,
  input  RST
);

  wire binary_to_bcd_converter_1_p4, n7_segment_display_1_p1, n7_segment_display_1_p2;
  wire [7:0] register_1_q;

  LED led_1 (.in(OI));
  LED led_2 (.in(CLK));
  Register register_1 (.D(BusIn), .en(OI), .clk(CLK), .Q(register_1_q), .clr(RST));
  LED led_3 (.in(RST));
  // _7_Segment_Display 7_segment_display_1: pin names not known; wires that end beside it: n7_segment_display_1_p1, n7_segment_display_1_p2
  // BCD_to_7_Segment_decoder bcd_to_7_segment_decoder_1: pin names not known
  // Binary_to_BCD_converter #(.binvalue(8)) binary_to_bcd_converter_1: pin names not known; wires that end beside it: register_1_q, n7_segment_display_1_p1, n7_segment_display_1_p2, binary_to_bcd_converter_1_p4
  // _7_Segment_Display 7_segment_display_2: pin names not known; wires that end beside it: n7_segment_display_1_p2, binary_to_bcd_converter_1_p4
  _7_Segment_Display u_7_segment_display_3 ();  // open: g, f, a, b, e, d, c, dp
  // BCD_to_7_Segment_decoder bcd_to_7_segment_decoder_2: pin names not known
  // BCD_to_7_Segment_decoder bcd_to_7_segment_decoder_3: pin names not known
endmodule

module ControlLogic (
  input  CLK,
  input  [7:0] BusOut,
  input  RST,
  input  [3:0] LogBusIn,
  input  CF,
  input  ZF,
  output AO,
  output AI,
  output II,
  output IO,
  output RO,
  output RI,
  output MI,
  output HLT,
  output FI,
  output J,
  output CO,
  output CE,
  output OI,
  output BI,
  output SU,
  output EO
);

  wire buffer_1_out, decoder_1_out0, decoder_1_out1, decoder_1_out2, decoder_1_out3, decoder_1_out4,
       nand_1_out, not_1_out;
  wire [2:0] counter_1_q;

  buf buffer_1 (buffer_1_out, RST);
  LED led_1 (.in(RST));
  Counter #(.max('h7), .width(3)) counter_1 (
    .clr(buffer_1_out), .clk(CLK), .Q(counter_1_q));  // open: load, up, count, D, carry
  LED led_2 (.in(CLK));
  LED led_3 (.in(counter_1_q[0]));
  LED led_4 (.in(counter_1_q[1]));
  LED led_5 (.in(counter_1_q[2]));
  LED led_6 (.in(CF));
  LED led_7 (.in(ZF));
  Decoder #(.enable("false"), .select(3)) decoder_1 (
    .out0(decoder_1_out0), .out1(decoder_1_out1), .out2(decoder_1_out2), .out3(decoder_1_out3),
    .out4(decoder_1_out4), .out5(buffer_1_out), .sel(counter_1_q));  // open: out6, out7
  ROM #(.addrWidth(11)) rom_1 (
    .addr({1'b0, ZF, CF, 1'b0, LogBusIn, counter_1_q}), .data({HLT, MI, RI, RO, IO, II, AI, AO}));
  ROM #(.addrWidth(11)) rom_2 (
    .addr({1'b0, ZF, CF, 1'b1, LogBusIn, counter_1_q}), .data({EO, SU, BI, OI, CE, CO, J, FI}));
  LED T4 (.in(decoder_1_out4));
  LED T3 (.in(decoder_1_out3));
  LED T2 (.in(decoder_1_out2));
  LED T1 (.in(decoder_1_out1));
  LED T0 (.in(decoder_1_out0));
  LED led_8 (.in(AO));
  LED led_9 (.in(AI));
  LED led_10 (.in(FI));
  LED led_11 (.in(J));
  LED led_12 (.in(II));
  LED led_13 (.in(CO));
  LED led_14 (.in(IO));
  LED led_15 (.in(RO));
  LED led_16 (.in(CE));
  LED led_17 (.in(OI));
  LED led_18 (.in(RI));
  LED led_19 (.in(BI));
  LED led_20 (.in(MI));
  LED led_21 (.in(HLT));
  LED led_22 (.in(SU));
  LED led_23 (.in(EO));
  nand nand_1 (nand_1_out, RO, RI, MI, HLT, AO, AI, II, IO, FI, J, CO, CE, OI, BI, SU, EO);
  assign BusOut = not_1_out ? {8{1'b0}} : 8'bz;  // Controlled_Buffer controlled_buffer_1
  not not_1 (not_1_out, nand_1_out);

  // Notes on the sheet:
  //   contents of rom_1 (hex, n*v repeats v):
  //   40 14 6*0 40 14 48 12 4*0 40 14 48 10 2 0 0 0 40 14 48 10 2 0 0 0 40 14 48 21 4*0 40 14 a 5*0 40 14
  //   8 5*0 40 14 6*0 40 14 6*0 40 14 6*0 40 14 6*0 40 14 6*0 40 14 6*0 40 14 6*0 40 14 1 5*0 40 14 80 5*0
  //   4 8 6*0 4 8 6*0 4 8 0 20 81 0 0 0 4 8 0 20 c1 0 0 0 4 8 6*0 4 8 6*0 4 8 2 5*0 4 8 6*0 4 8 6*0 4 8
  //   6*0 4 8 6*0 4 8 6*0 4 8 6*0 4 8 6*0 4 8 10 5*0 4 8 6*0 40 14 6*0 40 14 48 12 4*0 40 14 48 10 2 0 0 0
  //   40 14 48 10 2 0 0 0 40 14 48 21 4*0 40 14 a 5*0 40 14 8 5*0 40 14 8 5*0 40 14 6*0 40 14 6*0 40 14
  //   6*0 40 14 6*0 40 14 6*0 40 14 6*0 40 14 1 5*0 40 14 80 5*0 4 8 6*0 4 8 6*0 4 8 0 20 81 0 0 0 4 8 0
  //   20 c1 0 0 0 4 8 6*0 4 8 6*0 4 8 2 5*0 4 8 2 5*0 4 8 6*0 4 8 6*0 4 8 6*0 4 8 6*0 4 8 6*0 4 8 6*0 4 8
  //   10 5*0 4 8 6*0 40 14 6*0 40 14 48 12 4*0 40 14 48 10 2 0 0 0 40 14 48 10 2 0 0 0 40 14 48 21 4*0 40
  //   14 a 5*0 40 14 8 5*0 40 14 6*0 40 14 8 5*0 40 14 6*0 40 14 6*0 40 14 6*0 40 14 6*0 40 14 6*0 40 14 1
  //   5*0 40 14 80 5*0 4 8 6*0 4 8 6*0 4 8 0 20 81 0 0 0 4 8 0 20 c1 0 0 0 4 8 6*0 4 8 6*0 4 8 2 5*0 4 8
  //   6*0 4 8 2 5*0 4 8 6*0 4 8 6*0 4 8 6*0 4 8 6*0 4 8 6*0 4 8 10 5*0 4 8 6*0 40 14 6*0 40 14 48 12 4*0
  //   40 14 48 10 2 0 0 0 40 14 48 10 2 0 0 0 40 14 48 21 4*0 40 14 a 5*0 40 14 8 5*0 40 14 8 5*0 40 14 8
  //   5*0 40 14 6*0 40 14 6*0 40 14 6*0 40 14 6*0 40 14 6*0 40 14 1 5*0 40 14 80 5*0 4 8 6*0 4 8 6*0 4 8 0
  //   20 81 0 0 0 4 8 0 20 c1 0 0 0 4 8 6*0 4 8 6*0 4 8 2 5*0 4 8 2 5*0 4 8 2 5*0 4 8 6*0 4 8 6*0 4 8 6*0
  //   4 8 6*0 4 8 6*0 4 8 10 5*0 4 8
  //   contents of rom_2 (hex, n*v repeats v):
  //   40 14 6*0 40 14 48 12 4*0 40 14 48 10 2 0 0 0 40 14 48 10 2 0 0 0 40 14 48 21 4*0 40 14 a 5*0 40 14
  //   8 5*0 40 14 6*0 40 14 6*0 40 14 6*0 40 14 6*0 40 14 6*0 40 14 6*0 40 14 6*0 40 14 1 5*0 40 14 80 5*0
  //   4 8 6*0 4 8 6*0 4 8 0 20 81 0 0 0 4 8 0 20 c1 0 0 0 4 8 6*0 4 8 6*0 4 8 2 5*0 4 8 6*0 4 8 6*0 4 8
  //   6*0 4 8 6*0 4 8 6*0 4 8 6*0 4 8 6*0 4 8 10 5*0 4 8 6*0 40 14 6*0 40 14 48 12 4*0 40 14 48 10 2 0 0 0
  //   40 14 48 10 2 0 0 0 40 14 48 21 4*0 40 14 a 5*0 40 14 8 5*0 40 14 8 5*0 40 14 6*0 40 14 6*0 40 14
  //   6*0 40 14 6*0 40 14 6*0 40 14 6*0 40 14 1 5*0 40 14 80 5*0 4 8 6*0 4 8 6*0 4 8 0 20 81 0 0 0 4 8 0
  //   20 c1 0 0 0 4 8 6*0 4 8 6*0 4 8 2 5*0 4 8 2 5*0 4 8 6*0 4 8 6*0 4 8 6*0 4 8 6*0 4 8 6*0 4 8 6*0 4 8
  //   10 5*0 4 8 6*0 40 14 6*0 40 14 48 12 4*0 40 14 48 10 2 0 0 0 40 14 48 10 2 0 0 0 40 14 48 21 4*0 40
  //   14 a 5*0 40 14 8 5*0 40 14 6*0 40 14 8 5*0 40 14 6*0 40 14 6*0 40 14 6*0 40 14 6*0 40 14 6*0 40 14 1
  //   5*0 40 14 80 5*0 4 8 6*0 4 8 6*0 4 8 0 20 81 0 0 0 4 8 0 20 c1 0 0 0 4 8 6*0 4 8 6*0 4 8 2 5*0 4 8
  //   6*0 4 8 2 5*0 4 8 6*0 4 8 6*0 4 8 6*0 4 8 6*0 4 8 6*0 4 8 10 5*0 4 8 6*0 40 14 6*0 40 14 48 12 4*0
  //   40 14 48 10 2 0 0 0 40 14 48 10 2 0 0 0 40 14 48 21 4*0 40 14 a 5*0 40 14 8 5*0 40 14 8 5*0 40 14 8
  //   5*0 40 14 6*0 40 14 6*0 40 14 6*0 40 14 6*0 40 14 6*0 40 14 1 5*0 40 14 80 5*0 4 8 6*0 4 8 6*0 4 8 0
  //   20 81 0 0 0 4 8 0 20 c1 0 0 0 4 8 6*0 4 8 6*0 4 8 2 5*0 4 8 2 5*0 4 8 2 5*0 4 8 6*0 4 8 6*0 4 8 6*0
  //   4 8 6*0 4 8 6*0 4 8 10 5*0 4 8
endmodule
